// Logisim project cpu.circ as structural Verilog: 11 circuits, main circuit main
module main (
  input  in_1,
  output [31:0] Instr,
  output MemWrite,
  output [31:0] PC,
  output RegWrite,
  output [31:0] MemAddr,
  output [4:0] out_7,
  output [31:0] MemData,
  output [31:0] out_9
);

  wire alu_1_zero, BranchSel, Clk, controller_1_out_5, Counter, jalSel, SllOp, WDOp;
  wire [1:0] controller_1_out_6, controller_1_out_7, controller_1_out_8;
  wire [2:0] controller_1_out_3;
  wire [13:0] bit_extender_2_out;
  wire [27:0] bit_extender_1_out, jalPC;
  wire [31:0] adder_2_out, dm_1_rdb, dm_1_rdw, ext_1_signimm, ext_1_zeroimm, grf_1_rd1, multiplexer_1_out,
       multiplexer_2_out, multiplexer_5_out, PC_4, PC_prime_q, sll_1_sllimm;

  Clock clock_1 (.out(Clk));
  Counter #(.width(1), .max('h1), .ongoal("stay")) counter_1 (
    .Q(Counter), .clk(Clk), .clr(in_1));  // open: load, D, count, carry
  Multiplexer #(.width(32)) multiplexer_1 (
    .in0(PC_4), .in1(adder_2_out), .out(multiplexer_1_out), .sel(BranchSel));  // open: en
  Multiplexer #(.width(32)) multiplexer_2 (
    .in0(multiplexer_1_out), .in1({PC[31:28], jalPC}), .out(multiplexer_2_out), .sel(jalSel));  // open: en
  Register #(.width(32)) PC_prime (.D(multiplexer_2_out), .Q(PC_prime_q), .clk(Clk), .clr(in_1));  // open: en
  Multiplexer #(.width(32)) multiplexer_3 (.in0(32'h3000), .in1(PC_prime_q), .out(PC), .sel(Counter));  // open: en
  IFU ifu_1 (.Instr(Instr), .A(PC));
  Adder #(.width(32)) adder_1 (.a(PC), .b(32'h4), .out(PC_4));  // open: cin, cout
  assign bit_extender_1_out = {{2{1'b0}}, Instr[25:0]};  // Bit_Extender bit_extender_1
  Controller controller_1 (
    .Op(Instr[31:26]), .Funct(Instr[5:0]), .out_3(controller_1_out_3), .out_4(MemWrite),
    .out_5(controller_1_out_5), .out_6(controller_1_out_6), .out_7(controller_1_out_7),
    .out_8(controller_1_out_8), .out_9(RegWrite), .out_10(SllOp), .out_11(WDOp), .out_12(jalSel));
  GRF grf_1 (
    .clk(Clk), .reset(in_1), .WE(RegWrite), .A1(Instr[25:21]), .A2(Instr[20:16]), .A3(out_7), .WD(out_9),
    .RD1(grf_1_rd1), .RD2(MemData));
  Ext ext_1 (.Imm(Instr[15:0]), .ZeroImm(ext_1_zeroimm), .SignImm(ext_1_signimm));
  Sll sll_1 (.Imm(Instr[15:0]), .SllImm(sll_1_sllimm), .SllOp(SllOp));
  Shifter #(.width(28)) shifter_1 (.in(bit_extender_1_out), .\dist (5'b00010), .out(jalPC));
  Multiplexer #(.select(2), .width(5)) multiplexer_4 (
    .in0(Instr[20:16]), .in1(Instr[15:11]), .in2({5{1'b1}}), .out(out_7), .sel(controller_1_out_8));  // open: in3, en
  ALU alu_1 (
    .SrcA(grf_1_rd1), .SrcB(multiplexer_5_out), .SelOp(controller_1_out_6), .Zero(alu_1_zero),
    .ALUResult(MemAddr));
  Multiplexer #(.select(2), .width(32)) multiplexer_5 (
    .in0(MemData), .in1(ext_1_signimm), .in2(ext_1_zeroimm), .out(multiplexer_5_out), .sel(controller_1_out_7));  // open: in3, en
  Adder #(.width(32)) adder_2 (.a(PC_4), .b(sll_1_sllimm), .out(adder_2_out));  // open: cin, cout
  and and_1 (BranchSel, controller_1_out_5, alu_1_zero);
  Bit_Extender #(.in_width(32), .out_width(14)) bit_extender_2 (.in(MemAddr), .out(bit_extender_2_out));
  DM dm_1 (
    .A(bit_extender_2_out), .WD(MemData), .RDW(dm_1_rdw), .WE(MemWrite), .Clk(Clk), .Rst(in_1),
    .RDB(dm_1_rdb), .WDOp(WDOp));
  Multiplexer #(.select(3), .width(32)) multiplexer_6 (
    .in0(MemAddr), .in1(dm_1_rdw), .in2(sll_1_sllimm), .in3(dm_1_rdb), .in4(PC_4), .out(out_9),
    .sel(controller_1_out_3));  // open: in5, in6, in7, en
  // AND_Gate and_2 is placed but not wired

  // Other names for the same wires on the sheet: jalPC[31:28] = PC[31:28]; RegAddr[4:0] = out_7;
  //   RegData[31:0] = out_9; Rst = in_1

  // Notes on the sheet:
  //   PCPlus4
endmodule

module IFU (
  input  [31:0] A,
  output [31:0] Instr
);

  wire [11:0] bit_extender_1_out;
  wire [31:0] shifter_1_out, subtractor_1_out;

  Subtractor #(.width(32)) subtractor_1 (.a(A), .b(32'h3000), .out(subtractor_1_out));  // open: bin, bout
  Shifter #(.width(32), .shift("lr")) shifter_1 (.in(subtractor_1_out), .\dist (5'b00010), .out(shifter_1_out));
  Bit_Extender #(.in_width(32), .out_width(12)) bit_extender_1 (.in(shifter_1_out), .out(bit_extender_1_out));
  ROM #(.addrWidth(12), .dataWidth(32)) rom_1 (.addr(bit_extender_1_out), .data(Instr));  // open: sel
endmodule

module GRF (
  input  clk,
  input  reset,
  input  WE,
  input  [4:0] A1,
  input  [4:0] A2,
  input  [4:0] A3,
  input  [31:0] WD,
  output [31:0] RD1,
  output [31:0] RD2
);

  wire and_1_out, and_2_out, and_3_out, and_4_out, and_5_out, and_6_out, and_7_out, and_8_out, and_9_out,
       and_10_out, and_11_out, and_12_out, and_13_out, and_14_out, and_15_out, and_16_out, and_17_out,
       and_18_out, and_19_out, and_20_out, and_21_out, and_22_out, and_23_out, and_24_out, and_25_out,
       and_26_out, and_27_out, and_28_out, and_29_out, and_30_out, and_31_out, and_32_out, comparator_1_eq,
       comparator_2_eq, comparator_3_eq, comparator_4_eq, comparator_5_eq, comparator_6_eq, comparator_7_eq,
       comparator_8_eq, comparator_9_eq, comparator_10_eq, comparator_11_eq, comparator_12_eq,
       comparator_13_eq, comparator_14_eq, comparator_15_eq, comparator_16_eq, comparator_17_eq,
       comparator_18_eq, comparator_19_eq, comparator_20_eq, comparator_21_eq, comparator_22_eq,
       comparator_23_eq, comparator_24_eq, comparator_25_eq, comparator_26_eq, comparator_27_eq,
       comparator_28_eq, comparator_29_eq, comparator_30_eq, comparator_31_eq, comparator_32_eq,
       comparator_33_eq, comparator_34_eq, comparator_35_eq, comparator_36_eq, comparator_37_eq,
       comparator_38_eq, comparator_39_eq, comparator_40_eq, comparator_41_eq, comparator_42_eq,
       comparator_43_eq, comparator_44_eq, comparator_45_eq, comparator_46_eq, comparator_47_eq,
       comparator_48_eq, comparator_49_eq, comparator_50_eq, comparator_51_eq, comparator_52_eq,
       comparator_53_eq, comparator_54_eq, comparator_55_eq, comparator_56_eq, comparator_57_eq,
       comparator_58_eq, comparator_59_eq, comparator_60_eq, comparator_61_eq, comparator_62_eq,
       comparator_63_eq, comparator_64_eq, comparator_65_eq, comparator_66_eq, comparator_67_eq,
       comparator_68_eq, comparator_69_eq, comparator_70_eq, comparator_71_eq, comparator_72_eq,
       comparator_73_eq, comparator_74_eq, comparator_75_eq, comparator_76_eq, comparator_77_eq,
       comparator_78_eq, comparator_79_eq, comparator_80_eq, comparator_81_eq, comparator_82_eq,
       comparator_83_eq, comparator_84_eq, comparator_85_eq, comparator_86_eq, comparator_87_eq,
       comparator_88_eq, comparator_89_eq, comparator_90_eq, comparator_91_eq, comparator_92_eq,
       comparator_93_eq, comparator_94_eq, comparator_95_eq, comparator_96_eq;
  wire [31:0] _1_1, _1_2, _1_3, _1_4, _1_5, _1_6, _1_7, _1_8, _1a, _1b, _1c, _1d, _1e, _1f, _2_1, _2_2, _2_3,
       _2_4, _2_5, _2_6, _2_7, _2_8, _2a, _2b, _2c, _2d, _2e, _2f, _10, _11, _11a, _11b, _11c, _11d, _11e,
       _11f, _12, _13, _14, _15, _16, _17, _18, _19, _20, _21, _21a, _21b, _21c, _21d, _21e, _21f, _22, _23,
       _24, _25, _26, _27, _28, _29, _110, _111, _112, _113, _114, _115, _116, _117, _118, _119, _210, _211,
       _212, _213, _214, _215, _216, _217, _218, _219, bit_extender_1_out, bit_extender_2_out,
       bit_extender_3_out, bit_extender_4_out, bit_extender_5_out, bit_extender_6_out, bit_extender_7_out,
       bit_extender_8_out, bit_extender_9_out, bit_extender_10_out, bit_extender_11_out, bit_extender_12_out,
       bit_extender_13_out, bit_extender_14_out, bit_extender_15_out, bit_extender_16_out,
       bit_extender_17_out, bit_extender_18_out, bit_extender_19_out, bit_extender_20_out,
       bit_extender_21_out, bit_extender_22_out, bit_extender_23_out, bit_extender_24_out,
       bit_extender_25_out, bit_extender_26_out, bit_extender_27_out, bit_extender_28_out,
       bit_extender_29_out, bit_extender_30_out, bit_extender_31_out, bit_extender_32_out,
       bit_extender_33_out, bit_extender_34_out, bit_extender_35_out, bit_extender_36_out,
       bit_extender_37_out, bit_extender_38_out, bit_extender_39_out, bit_extender_40_out,
       bit_extender_41_out, bit_extender_42_out, bit_extender_43_out, bit_extender_44_out,
       bit_extender_45_out, bit_extender_46_out, bit_extender_47_out, bit_extender_48_out,
       bit_extender_49_out, bit_extender_50_out, bit_extender_51_out, bit_extender_52_out,
       bit_extender_53_out, bit_extender_54_out, bit_extender_55_out, bit_extender_56_out,
       bit_extender_57_out, bit_extender_58_out, bit_extender_59_out, bit_extender_60_out,
       bit_extender_61_out, bit_extender_62_out, bit_extender_63_out, bit_extender_64_out, register_1_q,
       register_2_q, register_3_q, register_4_q, register_5_q, register_6_q, register_7_q, register_8_q,
       register_9_q, register_10_q, register_11_q, register_12_q, register_13_q, register_14_q,
       register_15_q, register_16_q, register_17_q, register_18_q, register_19_q, register_20_q,
       register_21_q, register_22_q, register_23_q, register_24_q, register_25_q, register_26_q,
       register_27_q, register_28_q, register_29_q, register_30_q, register_31_q, register_32_q;

  assign _1_1 = _11 | _12 | _13 | _14 | _15;  // OR_Gate or_1, 32 bits wide
  assign _1_2 = _16 | _17 | _18 | _19 | _1a;  // OR_Gate or_2, 32 bits wide
  assign _1_3 = _1b | _1c | _1d | _1e | _1f;  // OR_Gate or_3, 32 bits wide
  assign _1_4 = _10 | _110 | _111 | _112 | _113;  // OR_Gate or_4, 32 bits wide
  assign _1_5 = _114 | _115 | _116 | _117 | _118;  // OR_Gate or_5, 32 bits wide
  assign _1_6 = _119 | _11a | _11b | _11c | _11d;  // OR_Gate or_6, 32 bits wide
  assign _1_7 = _11e | _11f;  // OR_Gate or_7, 32 bits wide
  assign _1_8 = _1_1 | _1_2 | _1_3 | _1_4 | _1_5;  // OR_Gate or_8, 32 bits wide
  assign RD1 = _1_6 | _1_7 | _1_8;  // OR_Gate or_9, 32 bits wide
  assign _2_1 = _21 | _22 | _23 | _24 | _25;  // OR_Gate or_10, 32 bits wide
  assign _2_2 = _26 | _27 | _28 | _29 | _2a;  // OR_Gate or_11, 32 bits wide
  assign _2_3 = _2b | _2c | _2d | _2e | _2f;  // OR_Gate or_12, 32 bits wide
  assign _2_4 = _20 | _210 | _211 | _212 | _213;  // OR_Gate or_13, 32 bits wide
  assign _2_5 = _214 | _215 | _216 | _217 | _218;  // OR_Gate or_14, 32 bits wide
  assign _2_6 = _219 | _21a | _21b | _21c | _21d;  // OR_Gate or_15, 32 bits wide
  assign _2_7 = _21e | _21f;  // OR_Gate or_16, 32 bits wide
  assign _2_8 = _2_1 | _2_2 | _2_3 | _2_4 | _2_5;  // OR_Gate or_17, 32 bits wide
  assign RD2 = _2_6 | _2_7 | _2_8;  // OR_Gate or_18, 32 bits wide
  Comparator #(.width(5), .mode("unsigned")) comparator_1 (
    .a(A3), .b({5{1'b0}}), .eq(comparator_1_eq));  // open: gt, lt
  Comparator #(.width(5), .mode("unsigned")) comparator_2 (.a(A3), .b(5'b00010), .eq(comparator_2_eq));  // open: gt, lt
  and and_1 (and_1_out, comparator_1_eq, WE);
  Comparator #(.width(5), .mode("unsigned")) comparator_3 (.a(A3), .b(5'b00001), .eq(comparator_3_eq));  // open: gt, lt
  and and_2 (and_2_out, comparator_3_eq, WE);
  and and_3 (and_3_out, comparator_2_eq, WE);
  Comparator #(.width(5), .mode("unsigned")) comparator_4 (.a(A3), .b(5'b00011), .eq(comparator_4_eq));  // open: gt, lt
  and and_4 (and_4_out, comparator_4_eq, WE);
  Comparator #(.width(5), .mode("unsigned")) comparator_5 (.a(A3), .b(5'b00100), .eq(comparator_5_eq));  // open: gt, lt
  Comparator #(.width(5), .mode("unsigned")) comparator_6 (.a(A3), .b(5'b00101), .eq(comparator_6_eq));  // open: gt, lt
  Comparator #(.width(5), .mode("unsigned")) comparator_7 (.a(A3), .b(5'b00110), .eq(comparator_7_eq));  // open: gt, lt
  Comparator #(.width(5), .mode("unsigned")) comparator_8 (.a(A3), .b(5'b00111), .eq(comparator_8_eq));  // open: gt, lt
  Comparator #(.width(5), .mode("unsigned")) comparator_9 (.a(A3), .b(5'b01000), .eq(comparator_9_eq));  // open: gt, lt
  Comparator #(.width(5), .mode("unsigned")) comparator_10 (
    .a(A3), .b(5'b01001), .eq(comparator_10_eq));  // open: gt, lt
  Comparator #(.width(5), .mode("unsigned")) comparator_11 (
    .a(A3), .b(5'b01010), .eq(comparator_11_eq));  // open: gt, lt
  Comparator #(.width(5), .mode("unsigned")) comparator_12 (
    .a(A3), .b(5'b01011), .eq(comparator_12_eq));  // open: gt, lt
  Comparator #(.width(5), .mode("unsigned")) comparator_13 (
    .a(A3), .b(5'b01100), .eq(comparator_13_eq));  // open: gt, lt
  Comparator #(.width(5), .mode("unsigned")) comparator_14 (
    .a(A3), .b(5'b01101), .eq(comparator_14_eq));  // open: gt, lt
  Comparator #(.width(5), .mode("unsigned")) comparator_15 (
    .a(A3), .b(5'b01110), .eq(comparator_15_eq));  // open: gt, lt
  Comparator #(.width(5), .mode("unsigned")) comparator_16 (
    .a(A3), .b(5'b01111), .eq(comparator_16_eq));  // open: gt, lt
  Comparator #(.width(5), .mode("unsigned")) comparator_17 (
    .a(A3), .b(5'b10000), .eq(comparator_17_eq));  // open: gt, lt
  Comparator #(.width(5), .mode("unsigned")) comparator_18 (
    .a(A3), .b(5'b10001), .eq(comparator_18_eq));  // open: gt, lt
  Comparator #(.width(5), .mode("unsigned")) comparator_19 (
    .a(A3), .b(5'b10010), .eq(comparator_19_eq));  // open: gt, lt
  Comparator #(.width(5), .mode("unsigned")) comparator_20 (
    .a(A3), .b(5'b10011), .eq(comparator_20_eq));  // open: gt, lt
  Comparator #(.width(5), .mode("unsigned")) comparator_21 (
    .a(A3), .b(5'b10100), .eq(comparator_21_eq));  // open: gt, lt
  Comparator #(.width(5), .mode("unsigned")) comparator_22 (
    .a(A3), .b(5'b10101), .eq(comparator_22_eq));  // open: gt, lt
  Comparator #(.width(5), .mode("unsigned")) comparator_23 (
    .a(A3), .b(5'b10110), .eq(comparator_23_eq));  // open: gt, lt
  Comparator #(.width(5), .mode("unsigned")) comparator_24 (
    .a(A3), .b(5'b10111), .eq(comparator_24_eq));  // open: gt, lt
  Comparator #(.width(5), .mode("unsigned")) comparator_25 (
    .a(A3), .b(5'b11000), .eq(comparator_25_eq));  // open: gt, lt
  Comparator #(.width(5), .mode("unsigned")) comparator_26 (
    .a(A3), .b(5'b11001), .eq(comparator_26_eq));  // open: gt, lt
  Comparator #(.width(5), .mode("unsigned")) comparator_27 (
    .a(A3), .b(5'b11010), .eq(comparator_27_eq));  // open: gt, lt
  Comparator #(.width(5), .mode("unsigned")) comparator_28 (
    .a(A3), .b(5'b11101), .eq(comparator_28_eq));  // open: gt, lt
  Register #(.width(32)) register_1 (.D(WD), .en(and_1_out), .Q(register_1_q), .clk(clk), .clr(1'b1));
  Register #(.width(32)) register_2 (.D(WD), .en(and_2_out), .Q(register_2_q), .clk(clk), .clr(reset));
  Register #(.width(32)) register_3 (.D(WD), .en(and_3_out), .Q(register_3_q), .clk(clk), .clr(reset));
  Register #(.width(32)) register_4 (.D(WD), .en(and_4_out), .Q(register_4_q), .clk(clk), .clr(reset));
  Register #(.width(32)) register_5 (.D(WD), .en(and_5_out), .Q(register_5_q), .clk(clk), .clr(reset));
  and and_5 (and_5_out, comparator_5_eq, WE);
  Register #(.width(32)) register_6 (.D(WD), .en(and_6_out), .Q(register_6_q), .clk(clk), .clr(reset));
  and and_6 (and_6_out, comparator_6_eq, WE);
  Register #(.width(32)) register_7 (.D(WD), .en(and_7_out), .Q(register_7_q), .clk(clk), .clr(reset));
  and and_7 (and_7_out, comparator_7_eq, WE);
  and and_8 (and_8_out, comparator_8_eq, WE);
  and and_9 (and_9_out, comparator_9_eq, WE);
  and and_10 (and_10_out, comparator_10_eq, WE);
  and and_11 (and_11_out, comparator_11_eq, WE);
  and and_12 (and_12_out, comparator_12_eq, WE);
  and and_13 (and_13_out, comparator_13_eq, WE);
  and and_14 (and_14_out, comparator_14_eq, WE);
  and and_15 (and_15_out, comparator_15_eq, WE);
  and and_16 (and_16_out, comparator_16_eq, WE);
  and and_17 (and_17_out, comparator_17_eq, WE);
  and and_18 (and_18_out, comparator_18_eq, WE);
  and and_19 (and_19_out, comparator_19_eq, WE);
  and and_20 (and_20_out, comparator_20_eq, WE);
  and and_21 (and_21_out, comparator_21_eq, WE);
  and and_22 (and_22_out, comparator_22_eq, WE);
  and and_23 (and_23_out, comparator_23_eq, WE);
  and and_24 (and_24_out, comparator_24_eq, WE);
  and and_25 (and_25_out, comparator_25_eq, WE);
  and and_26 (and_26_out, comparator_26_eq, WE);
  and and_27 (and_27_out, comparator_27_eq, WE);
  Comparator #(.width(5), .mode("unsigned")) comparator_29 (
    .a(A3), .b(5'b11011), .eq(comparator_29_eq));  // open: gt, lt
  and and_28 (and_28_out, comparator_29_eq, WE);
  Comparator #(.width(5), .mode("unsigned")) comparator_30 (
    .a(A3), .b(5'b11100), .eq(comparator_30_eq));  // open: gt, lt
  and and_29 (and_29_out, comparator_30_eq, WE);
  and and_30 (and_30_out, comparator_28_eq, WE);
  Comparator #(.width(5), .mode("unsigned")) comparator_31 (
    .a(A3), .b(5'b11110), .eq(comparator_31_eq));  // open: gt, lt
  and and_31 (and_31_out, comparator_31_eq, WE);
  Comparator #(.width(5), .mode("unsigned")) comparator_32 (
    .a(A3), .b({5{1'b1}}), .eq(comparator_32_eq));  // open: gt, lt
  and and_32 (and_32_out, comparator_32_eq, WE);
  Register #(.width(32)) register_8 (.D(WD), .en(and_8_out), .Q(register_8_q), .clk(clk), .clr(reset));
  Register #(.width(32)) register_9 (.D(WD), .en(and_9_out), .Q(register_9_q), .clk(clk), .clr(reset));
  Register #(.width(32)) register_10 (.D(WD), .en(and_10_out), .Q(register_10_q), .clk(clk), .clr(reset));
  Register #(.width(32)) register_11 (.D(WD), .en(and_11_out), .Q(register_11_q), .clk(clk), .clr(reset));
  Register #(.width(32)) register_12 (.D(WD), .en(and_12_out), .Q(register_12_q), .clk(clk), .clr(reset));
  Register #(.width(32)) register_13 (.D(WD), .en(and_13_out), .Q(register_13_q), .clk(clk), .clr(reset));
  Register #(.width(32)) register_14 (.D(WD), .en(and_14_out), .Q(register_14_q), .clk(clk), .clr(reset));
  Register #(.width(32)) register_15 (.D(WD), .en(and_15_out), .Q(register_15_q), .clk(clk), .clr(reset));
  Register #(.width(32)) register_16 (.D(WD), .en(and_16_out), .Q(register_16_q), .clk(clk), .clr(reset));
  Register #(.width(32)) register_17 (.D(WD), .en(and_17_out), .Q(register_17_q), .clk(clk), .clr(reset));
  Register #(.width(32)) register_18 (.D(WD), .en(and_18_out), .Q(register_18_q), .clk(clk), .clr(reset));
  Register #(.width(32)) register_19 (.D(WD), .en(and_19_out), .Q(register_19_q), .clk(clk), .clr(reset));
  Register #(.width(32)) register_20 (.D(WD), .en(and_20_out), .Q(register_20_q), .clk(clk), .clr(reset));
  Register #(.width(32)) register_21 (.D(WD), .en(and_21_out), .Q(register_21_q), .clk(clk), .clr(reset));
  Register #(.width(32)) register_22 (.D(WD), .en(and_22_out), .Q(register_22_q), .clk(clk), .clr(reset));
  Register #(.width(32)) register_23 (.D(WD), .en(and_23_out), .Q(register_23_q), .clk(clk), .clr(reset));
  Register #(.width(32)) register_24 (.D(WD), .en(and_24_out), .Q(register_24_q), .clk(clk), .clr(reset));
  Register #(.width(32)) register_25 (.D(WD), .en(and_25_out), .Q(register_25_q), .clk(clk), .clr(reset));
  Register #(.width(32)) register_26 (.D(WD), .en(and_26_out), .Q(register_26_q), .clk(clk), .clr(reset));
  Register #(.width(32)) register_27 (.D(WD), .en(and_27_out), .Q(register_27_q), .clk(clk), .clr(reset));
  Register #(.width(32)) register_28 (.D(WD), .en(and_28_out), .Q(register_28_q), .clk(clk), .clr(reset));
  Register #(.width(32)) register_29 (.D(WD), .en(and_29_out), .Q(register_29_q), .clk(clk), .clr(reset));
  Register #(.width(32)) register_30 (.D(WD), .en(and_30_out), .Q(register_30_q), .clk(clk), .clr(reset));
  Register #(.width(32)) register_31 (.D(WD), .en(and_31_out), .Q(register_31_q), .clk(clk), .clr(reset));
  Register #(.width(32)) register_32 (.D(WD), .en(and_32_out), .Q(register_32_q), .clk(clk), .clr(reset));
  Comparator #(.width(5), .mode("unsigned")) comparator_33 (
    .a(A1), .b({5{1'b0}}), .eq(comparator_33_eq));  // open: gt, lt
  Comparator #(.width(5), .mode("unsigned")) comparator_34 (
    .a(A2), .b({5{1'b0}}), .eq(comparator_34_eq));  // open: gt, lt
  Comparator #(.width(5), .mode("unsigned")) comparator_35 (
    .a(A1), .b(5'b00001), .eq(comparator_35_eq));  // open: gt, lt
  Comparator #(.width(5), .mode("unsigned")) comparator_36 (
    .a(A2), .b(5'b00001), .eq(comparator_36_eq));  // open: gt, lt
  Comparator #(.width(5), .mode("unsigned")) comparator_37 (
    .a(A1), .b(5'b00010), .eq(comparator_37_eq));  // open: gt, lt
  Comparator #(.width(5), .mode("unsigned")) comparator_38 (
    .a(A2), .b(5'b00010), .eq(comparator_38_eq));  // open: gt, lt
  Comparator #(.width(5), .mode("unsigned")) comparator_39 (
    .a(A1), .b(5'b00011), .eq(comparator_39_eq));  // open: gt, lt
  Comparator #(.width(5), .mode("unsigned")) comparator_40 (
    .a(A2), .b(5'b00011), .eq(comparator_40_eq));  // open: gt, lt
  Comparator #(.width(5), .mode("unsigned")) comparator_41 (
    .a(A1), .b(5'b00100), .eq(comparator_41_eq));  // open: gt, lt
  Comparator #(.width(5), .mode("unsigned")) comparator_42 (
    .a(A2), .b(5'b00100), .eq(comparator_42_eq));  // open: gt, lt
  Comparator #(.width(5), .mode("unsigned")) comparator_43 (
    .a(A1), .b(5'b00101), .eq(comparator_43_eq));  // open: gt, lt
  Comparator #(.width(5), .mode("unsigned")) comparator_44 (
    .a(A2), .b(5'b00101), .eq(comparator_44_eq));  // open: gt, lt
  Comparator #(.width(5), .mode("unsigned")) comparator_45 (
    .a(A1), .b(5'b00110), .eq(comparator_45_eq));  // open: gt, lt
  Comparator #(.width(5), .mode("unsigned")) comparator_46 (
    .a(A2), .b(5'b00110), .eq(comparator_46_eq));  // open: gt, lt
  Comparator #(.width(5), .mode("unsigned")) comparator_47 (
    .a(A1), .b(5'b00111), .eq(comparator_47_eq));  // open: gt, lt
  Comparator #(.width(5), .mode("unsigned")) comparator_48 (
    .a(A2), .b(5'b00111), .eq(comparator_48_eq));  // open: gt, lt
  Comparator #(.width(5), .mode("unsigned")) comparator_49 (
    .a(A1), .b(5'b01000), .eq(comparator_49_eq));  // open: gt, lt
  Comparator #(.width(5), .mode("unsigned")) comparator_50 (
    .a(A2), .b(5'b01000), .eq(comparator_50_eq));  // open: gt, lt
  Comparator #(.width(5), .mode("unsigned")) comparator_51 (
    .a(A1), .b(5'b01001), .eq(comparator_51_eq));  // open: gt, lt
  Comparator #(.width(5), .mode("unsigned")) comparator_52 (
    .a(A2), .b(5'b01001), .eq(comparator_52_eq));  // open: gt, lt
  Comparator #(.width(5), .mode("unsigned")) comparator_53 (
    .a(A1), .b(5'b01010), .eq(comparator_53_eq));  // open: gt, lt
  Comparator #(.width(5), .mode("unsigned")) comparator_54 (
    .a(A2), .b(5'b01010), .eq(comparator_54_eq));  // open: gt, lt
  Comparator #(.width(5), .mode("unsigned")) comparator_55 (
    .a(A1), .b(5'b01011), .eq(comparator_55_eq));  // open: gt, lt
  Comparator #(.width(5), .mode("unsigned")) comparator_56 (
    .a(A2), .b(5'b01011), .eq(comparator_56_eq));  // open: gt, lt
  Comparator #(.width(5), .mode("unsigned")) comparator_57 (
    .a(A1), .b(5'b01100), .eq(comparator_57_eq));  // open: gt, lt
  Comparator #(.width(5), .mode("unsigned")) comparator_58 (
    .a(A2), .b(5'b01100), .eq(comparator_58_eq));  // open: gt, lt
  Comparator #(.width(5), .mode("unsigned")) comparator_59 (
    .a(A2), .b(5'b01101), .eq(comparator_59_eq));  // open: gt, lt
  Comparator #(.width(5), .mode("unsigned")) comparator_60 (
    .a(A2), .b(5'b01110), .eq(comparator_60_eq));  // open: gt, lt
  Comparator #(.width(5), .mode("unsigned")) comparator_61 (
    .a(A2), .b(5'b01111), .eq(comparator_61_eq));  // open: gt, lt
  Comparator #(.width(5), .mode("unsigned")) comparator_62 (
    .a(A2), .b(5'b10101), .eq(comparator_62_eq));  // open: gt, lt
  assign bit_extender_1_out = {{31{comparator_33_eq}}, comparator_33_eq};  // Bit_Extender bit_extender_1
  assign _20 = register_1_q & bit_extender_2_out;  // AND_Gate and_33, 32 bits wide
  assign bit_extender_2_out = {{31{comparator_34_eq}}, comparator_34_eq};  // Bit_Extender bit_extender_2
  assign bit_extender_3_out = {{31{comparator_35_eq}}, comparator_35_eq};  // Bit_Extender bit_extender_3
  assign bit_extender_4_out = {{31{comparator_36_eq}}, comparator_36_eq};  // Bit_Extender bit_extender_4
  assign bit_extender_5_out = {{31{comparator_37_eq}}, comparator_37_eq};  // Bit_Extender bit_extender_5
  assign _22 = register_3_q & bit_extender_6_out;  // AND_Gate and_34, 32 bits wide
  assign bit_extender_6_out = {{31{comparator_38_eq}}, comparator_38_eq};  // Bit_Extender bit_extender_6
  assign bit_extender_7_out = {{31{comparator_39_eq}}, comparator_39_eq};  // Bit_Extender bit_extender_7
  assign bit_extender_8_out = {{31{comparator_40_eq}}, comparator_40_eq};  // Bit_Extender bit_extender_8
  assign bit_extender_9_out = {{31{comparator_41_eq}}, comparator_41_eq};  // Bit_Extender bit_extender_9
  assign bit_extender_10_out = {{31{comparator_42_eq}}, comparator_42_eq};  // Bit_Extender bit_extender_10
  assign bit_extender_11_out = {{31{comparator_43_eq}}, comparator_43_eq};  // Bit_Extender bit_extender_11
  assign bit_extender_12_out = {{31{comparator_44_eq}}, comparator_44_eq};  // Bit_Extender bit_extender_12
  assign bit_extender_13_out = {{31{comparator_45_eq}}, comparator_45_eq};  // Bit_Extender bit_extender_13
  assign bit_extender_14_out = {{31{comparator_46_eq}}, comparator_46_eq};  // Bit_Extender bit_extender_14
  assign bit_extender_15_out = {{31{comparator_47_eq}}, comparator_47_eq};  // Bit_Extender bit_extender_15
  assign bit_extender_16_out = {{31{comparator_48_eq}}, comparator_48_eq};  // Bit_Extender bit_extender_16
  assign bit_extender_17_out = {{31{comparator_49_eq}}, comparator_49_eq};  // Bit_Extender bit_extender_17
  assign bit_extender_18_out = {{31{comparator_50_eq}}, comparator_50_eq};  // Bit_Extender bit_extender_18
  assign bit_extender_19_out = {{31{comparator_51_eq}}, comparator_51_eq};  // Bit_Extender bit_extender_19
  assign bit_extender_20_out = {{31{comparator_52_eq}}, comparator_52_eq};  // Bit_Extender bit_extender_20
  assign bit_extender_21_out = {{31{comparator_53_eq}}, comparator_53_eq};  // Bit_Extender bit_extender_21
  assign bit_extender_22_out = {{31{comparator_54_eq}}, comparator_54_eq};  // Bit_Extender bit_extender_22
  assign bit_extender_23_out = {{31{comparator_55_eq}}, comparator_55_eq};  // Bit_Extender bit_extender_23
  assign bit_extender_24_out = {{31{comparator_56_eq}}, comparator_56_eq};  // Bit_Extender bit_extender_24
  assign bit_extender_25_out = {{31{comparator_57_eq}}, comparator_57_eq};  // Bit_Extender bit_extender_25
  assign bit_extender_26_out = {{31{comparator_58_eq}}, comparator_58_eq};  // Bit_Extender bit_extender_26
  assign bit_extender_27_out = {{31{comparator_63_eq}}, comparator_63_eq};  // Bit_Extender bit_extender_27
  Comparator #(.width(5), .mode("unsigned")) comparator_63 (
    .a(A1), .b(5'b01101), .eq(comparator_63_eq));  // open: gt, lt
  assign bit_extender_28_out = {{31{comparator_59_eq}}, comparator_59_eq};  // Bit_Extender bit_extender_28
  Comparator #(.width(5), .mode("unsigned")) comparator_64 (
    .a(A1), .b(5'b01110), .eq(comparator_64_eq));  // open: gt, lt
  assign bit_extender_29_out = {{31{comparator_64_eq}}, comparator_64_eq};  // Bit_Extender bit_extender_29
  assign bit_extender_30_out = {{31{comparator_60_eq}}, comparator_60_eq};  // Bit_Extender bit_extender_30
  Comparator #(.width(5), .mode("unsigned")) comparator_65 (
    .a(A1), .b(5'b01111), .eq(comparator_65_eq));  // open: gt, lt
  assign bit_extender_31_out = {{31{comparator_65_eq}}, comparator_65_eq};  // Bit_Extender bit_extender_31
  assign bit_extender_32_out = {{31{comparator_61_eq}}, comparator_61_eq};  // Bit_Extender bit_extender_32
  assign bit_extender_33_out = {{31{comparator_66_eq}}, comparator_66_eq};  // Bit_Extender bit_extender_33
  Comparator #(.width(5), .mode("unsigned")) comparator_66 (
    .a(A1), .b(5'b10000), .eq(comparator_66_eq));  // open: gt, lt
  Comparator #(.width(5), .mode("unsigned")) comparator_67 (
    .a(A2), .b(5'b10000), .eq(comparator_67_eq));  // open: gt, lt
  assign bit_extender_34_out = {{31{comparator_67_eq}}, comparator_67_eq};  // Bit_Extender bit_extender_34
  Comparator #(.width(5), .mode("unsigned")) comparator_68 (
    .a(A1), .b(5'b10001), .eq(comparator_68_eq));  // open: gt, lt
  Comparator #(.width(5), .mode("unsigned")) comparator_69 (
    .a(A2), .b(5'b10001), .eq(comparator_69_eq));  // open: gt, lt
  assign bit_extender_35_out = {{31{comparator_69_eq}}, comparator_69_eq};  // Bit_Extender bit_extender_35
  Comparator #(.width(5), .mode("unsigned")) comparator_70 (
    .a(A1), .b(5'b10010), .eq(comparator_70_eq));  // open: gt, lt
  assign bit_extender_36_out = {{31{comparator_71_eq}}, comparator_71_eq};  // Bit_Extender bit_extender_36
  Comparator #(.width(5), .mode("unsigned")) comparator_71 (
    .a(A2), .b(5'b10010), .eq(comparator_71_eq));  // open: gt, lt
  assign bit_extender_37_out = {{31{comparator_72_eq}}, comparator_72_eq};  // Bit_Extender bit_extender_37
  Comparator #(.width(5), .mode("unsigned")) comparator_72 (
    .a(A1), .b(5'b10011), .eq(comparator_72_eq));  // open: gt, lt
  assign bit_extender_38_out = {{31{comparator_73_eq}}, comparator_73_eq};  // Bit_Extender bit_extender_38
  Comparator #(.width(5), .mode("unsigned")) comparator_73 (
    .a(A2), .b(5'b10011), .eq(comparator_73_eq));  // open: gt, lt
  Comparator #(.width(5), .mode("unsigned")) comparator_74 (
    .a(A1), .b(5'b10100), .eq(comparator_74_eq));  // open: gt, lt
  assign bit_extender_39_out = {{31{comparator_74_eq}}, comparator_74_eq};  // Bit_Extender bit_extender_39
  Comparator #(.width(5), .mode("unsigned")) comparator_75 (
    .a(A2), .b(5'b10100), .eq(comparator_75_eq));  // open: gt, lt
  assign bit_extender_40_out = {{31{comparator_75_eq}}, comparator_75_eq};  // Bit_Extender bit_extender_40
  Comparator #(.width(5), .mode("unsigned")) comparator_76 (
    .a(A1), .b(5'b10101), .eq(comparator_76_eq));  // open: gt, lt
  assign bit_extender_41_out = {{31{comparator_76_eq}}, comparator_76_eq};  // Bit_Extender bit_extender_41
  assign bit_extender_42_out = {{31{comparator_62_eq}}, comparator_62_eq};  // Bit_Extender bit_extender_42
  Comparator #(.width(5), .mode("unsigned")) comparator_77 (
    .a(A1), .b(5'b10110), .eq(comparator_77_eq));  // open: gt, lt
  assign bit_extender_43_out = {{31{comparator_77_eq}}, comparator_77_eq};  // Bit_Extender bit_extender_43
  assign bit_extender_44_out = {{31{comparator_78_eq}}, comparator_78_eq};  // Bit_Extender bit_extender_44
  Comparator #(.width(5), .mode("unsigned")) comparator_78 (
    .a(A2), .b(5'b10110), .eq(comparator_78_eq));  // open: gt, lt
  Comparator #(.width(5), .mode("unsigned")) comparator_79 (
    .a(A1), .b(5'b10111), .eq(comparator_79_eq));  // open: gt, lt
  Comparator #(.width(5), .mode("unsigned")) comparator_80 (
    .a(A2), .b(5'b10111), .eq(comparator_80_eq));  // open: gt, lt
  assign bit_extender_45_out = {{31{comparator_80_eq}}, comparator_80_eq};  // Bit_Extender bit_extender_45
  Comparator #(.width(5), .mode("unsigned")) comparator_81 (
    .a(A1), .b(5'b11000), .eq(comparator_81_eq));  // open: gt, lt
  Comparator #(.width(5), .mode("unsigned")) comparator_82 (
    .a(A2), .b(5'b11000), .eq(comparator_82_eq));  // open: gt, lt
  assign bit_extender_46_out = {{31{comparator_82_eq}}, comparator_82_eq};  // Bit_Extender bit_extender_46
  Comparator #(.width(5), .mode("unsigned")) comparator_83 (
    .a(A1), .b(5'b11001), .eq(comparator_83_eq));  // open: gt, lt
  assign bit_extender_47_out = {{31{comparator_84_eq}}, comparator_84_eq};  // Bit_Extender bit_extender_47
  Comparator #(.width(5), .mode("unsigned")) comparator_84 (
    .a(A2), .b(5'b11001), .eq(comparator_84_eq));  // open: gt, lt
  Comparator #(.width(5), .mode("unsigned")) comparator_85 (
    .a(A1), .b(5'b11010), .eq(comparator_85_eq));  // open: gt, lt
  Comparator #(.width(5), .mode("unsigned")) comparator_86 (
    .a(A2), .b(5'b11010), .eq(comparator_86_eq));  // open: gt, lt
  Comparator #(.width(5), .mode("unsigned")) comparator_87 (
    .a(A1), .b(5'b11011), .eq(comparator_87_eq));  // open: gt, lt
  Comparator #(.width(5), .mode("unsigned")) comparator_88 (
    .a(A2), .b(5'b11011), .eq(comparator_88_eq));  // open: gt, lt
  Comparator #(.width(5), .mode("unsigned")) comparator_89 (
    .a(A1), .b(5'b11100), .eq(comparator_89_eq));  // open: gt, lt
  Comparator #(.width(5), .mode("unsigned")) comparator_90 (
    .a(A2), .b(5'b11100), .eq(comparator_90_eq));  // open: gt, lt
  Comparator #(.width(5), .mode("unsigned")) comparator_91 (
    .a(A1), .b(5'b11101), .eq(comparator_91_eq));  // open: gt, lt
  Comparator #(.width(5), .mode("unsigned")) comparator_92 (
    .a(A2), .b(5'b11101), .eq(comparator_92_eq));  // open: gt, lt
  Comparator #(.width(5), .mode("unsigned")) comparator_93 (
    .a(A1), .b(5'b11110), .eq(comparator_93_eq));  // open: gt, lt
  Comparator #(.width(5), .mode("unsigned")) comparator_94 (
    .a(A2), .b(5'b11110), .eq(comparator_94_eq));  // open: gt, lt
  Comparator #(.width(5), .mode("unsigned")) comparator_95 (
    .a(A1), .b({5{1'b1}}), .eq(comparator_95_eq));  // open: gt, lt
  Comparator #(.width(5), .mode("unsigned")) comparator_96 (
    .a(A2), .b({5{1'b1}}), .eq(comparator_96_eq));  // open: gt, lt
  assign _10 = bit_extender_1_out & register_1_q;  // AND_Gate and_35, 32 bits wide
  assign _11 = bit_extender_3_out & register_2_q;  // AND_Gate and_36, 32 bits wide
  assign _21 = register_2_q & bit_extender_4_out;  // AND_Gate and_37, 32 bits wide
  assign _12 = bit_extender_5_out & register_3_q;  // AND_Gate and_38, 32 bits wide
  assign _13 = bit_extender_7_out & register_4_q;  // AND_Gate and_39, 32 bits wide
  assign _23 = register_4_q & bit_extender_8_out;  // AND_Gate and_40, 32 bits wide
  assign _14 = bit_extender_9_out & register_5_q;  // AND_Gate and_41, 32 bits wide
  assign _24 = register_5_q & bit_extender_10_out;  // AND_Gate and_42, 32 bits wide
  assign _15 = bit_extender_11_out & register_6_q;  // AND_Gate and_43, 32 bits wide
  assign _25 = register_6_q & bit_extender_12_out;  // AND_Gate and_44, 32 bits wide
  assign _16 = bit_extender_13_out & register_7_q;  // AND_Gate and_45, 32 bits wide
  assign _26 = register_7_q & bit_extender_14_out;  // AND_Gate and_46, 32 bits wide
  assign _17 = bit_extender_15_out & register_8_q;  // AND_Gate and_47, 32 bits wide
  assign _27 = register_8_q & bit_extender_16_out;  // AND_Gate and_48, 32 bits wide
  assign _18 = bit_extender_17_out & register_9_q;  // AND_Gate and_49, 32 bits wide
  assign _28 = register_9_q & bit_extender_18_out;  // AND_Gate and_50, 32 bits wide
  assign _19 = bit_extender_19_out & register_10_q;  // AND_Gate and_51, 32 bits wide
  assign _29 = register_10_q & bit_extender_20_out;  // AND_Gate and_52, 32 bits wide
  assign _1a = bit_extender_21_out & register_11_q;  // AND_Gate and_53, 32 bits wide
  assign _2a = register_11_q & bit_extender_22_out;  // AND_Gate and_54, 32 bits wide
  assign _1b = bit_extender_23_out & register_12_q;  // AND_Gate and_55, 32 bits wide
  assign _2b = register_12_q & bit_extender_24_out;  // AND_Gate and_56, 32 bits wide
  assign _1c = bit_extender_25_out & register_13_q;  // AND_Gate and_57, 32 bits wide
  assign _2c = register_13_q & bit_extender_26_out;  // AND_Gate and_58, 32 bits wide
  assign _1d = bit_extender_27_out & register_14_q;  // AND_Gate and_59, 32 bits wide
  assign _2d = register_14_q & bit_extender_28_out;  // AND_Gate and_60, 32 bits wide
  assign _1e = bit_extender_29_out & register_15_q;  // AND_Gate and_61, 32 bits wide
  assign _2e = register_15_q & bit_extender_30_out;  // AND_Gate and_62, 32 bits wide
  assign _1f = bit_extender_31_out & register_16_q;  // AND_Gate and_63, 32 bits wide
  assign _2f = register_16_q & bit_extender_32_out;  // AND_Gate and_64, 32 bits wide
  assign _110 = bit_extender_33_out & register_17_q;  // AND_Gate and_65, 32 bits wide
  assign _210 = register_17_q & bit_extender_34_out;  // AND_Gate and_66, 32 bits wide
  assign bit_extender_48_out = {{31{comparator_68_eq}}, comparator_68_eq};  // Bit_Extender bit_extender_48
  assign _111 = bit_extender_48_out & register_18_q;  // AND_Gate and_67, 32 bits wide
  assign _211 = register_18_q & bit_extender_35_out;  // AND_Gate and_68, 32 bits wide
  assign bit_extender_49_out = {{31{comparator_70_eq}}, comparator_70_eq};  // Bit_Extender bit_extender_49
  assign _112 = bit_extender_49_out & register_19_q;  // AND_Gate and_69, 32 bits wide
  assign _212 = register_19_q & bit_extender_36_out;  // AND_Gate and_70, 32 bits wide
  assign _113 = bit_extender_37_out & register_20_q;  // AND_Gate and_71, 32 bits wide
  assign _213 = register_20_q & bit_extender_38_out;  // AND_Gate and_72, 32 bits wide
  assign _114 = bit_extender_39_out & register_21_q;  // AND_Gate and_73, 32 bits wide
  assign _214 = register_21_q & bit_extender_40_out;  // AND_Gate and_74, 32 bits wide
  assign _115 = bit_extender_41_out & register_22_q;  // AND_Gate and_75, 32 bits wide
  assign _215 = register_22_q & bit_extender_42_out;  // AND_Gate and_76, 32 bits wide
  assign _116 = bit_extender_43_out & register_23_q;  // AND_Gate and_77, 32 bits wide
  assign _216 = register_23_q & bit_extender_44_out;  // AND_Gate and_78, 32 bits wide
  assign bit_extender_50_out = {{31{comparator_79_eq}}, comparator_79_eq};  // Bit_Extender bit_extender_50
  assign _117 = bit_extender_50_out & register_24_q;  // AND_Gate and_79, 32 bits wide
  assign _217 = register_24_q & bit_extender_45_out;  // AND_Gate and_80, 32 bits wide
  assign bit_extender_51_out = {{31{comparator_81_eq}}, comparator_81_eq};  // Bit_Extender bit_extender_51
  assign _118 = bit_extender_51_out & register_25_q;  // AND_Gate and_81, 32 bits wide
  assign _218 = register_25_q & bit_extender_46_out;  // AND_Gate and_82, 32 bits wide
  assign bit_extender_52_out = {{31{comparator_83_eq}}, comparator_83_eq};  // Bit_Extender bit_extender_52
  assign _119 = bit_extender_52_out & register_26_q;  // AND_Gate and_83, 32 bits wide
  assign _219 = register_26_q & bit_extender_47_out;  // AND_Gate and_84, 32 bits wide
  assign bit_extender_53_out = {{31{comparator_85_eq}}, comparator_85_eq};  // Bit_Extender bit_extender_53
  assign _21a = register_27_q & bit_extender_54_out;  // AND_Gate and_85, 32 bits wide
  assign bit_extender_54_out = {{31{comparator_86_eq}}, comparator_86_eq};  // Bit_Extender bit_extender_54
  assign bit_extender_55_out = {{31{comparator_87_eq}}, comparator_87_eq};  // Bit_Extender bit_extender_55
  assign bit_extender_56_out = {{31{comparator_88_eq}}, comparator_88_eq};  // Bit_Extender bit_extender_56
  assign bit_extender_57_out = {{31{comparator_89_eq}}, comparator_89_eq};  // Bit_Extender bit_extender_57
  assign bit_extender_58_out = {{31{comparator_90_eq}}, comparator_90_eq};  // Bit_Extender bit_extender_58
  assign bit_extender_59_out = {{31{comparator_91_eq}}, comparator_91_eq};  // Bit_Extender bit_extender_59
  assign _21d = register_30_q & bit_extender_60_out;  // AND_Gate and_86, 32 bits wide
  assign bit_extender_60_out = {{31{comparator_92_eq}}, comparator_92_eq};  // Bit_Extender bit_extender_60
  assign bit_extender_61_out = {{31{comparator_93_eq}}, comparator_93_eq};  // Bit_Extender bit_extender_61
  assign bit_extender_62_out = {{31{comparator_94_eq}}, comparator_94_eq};  // Bit_Extender bit_extender_62
  assign bit_extender_63_out = {{31{comparator_95_eq}}, comparator_95_eq};  // Bit_Extender bit_extender_63
  assign bit_extender_64_out = {{31{comparator_96_eq}}, comparator_96_eq};  // Bit_Extender bit_extender_64
  assign _11a = bit_extender_53_out & register_27_q;  // AND_Gate and_87, 32 bits wide
  assign _11b = bit_extender_55_out & register_28_q;  // AND_Gate and_88, 32 bits wide
  assign _21b = register_28_q & bit_extender_56_out;  // AND_Gate and_89, 32 bits wide
  assign _11c = bit_extender_57_out & register_29_q;  // AND_Gate and_90, 32 bits wide
  assign _21c = register_29_q & bit_extender_58_out;  // AND_Gate and_91, 32 bits wide
  assign _11d = bit_extender_59_out & register_30_q;  // AND_Gate and_92, 32 bits wide
  assign _11e = bit_extender_61_out & register_31_q;  // AND_Gate and_93, 32 bits wide
  assign _21e = register_31_q & bit_extender_62_out;  // AND_Gate and_94, 32 bits wide
  assign _11f = bit_extender_63_out & register_32_q;  // AND_Gate and_95, 32 bits wide
  assign _21f = register_32_q & bit_extender_64_out;  // AND_Gate and_96, 32 bits wide
endmodule

module DM (
  input  [13:0] A,
  input  [31:0] WD,
  input  WDOp,
  input  WE,
  input  Clk,
  input  Rst,
  output [31:0] RDW,
  output [31:0] RDB
);

  wire [1:0] bit_extender_1_out, bit_extender_4_out, subtractor_1_out;
  wire [7:0] bitselector_1_out;
  wire [11:0] bit_extender_3_out;
  wire [13:0] shifter_1_out;
  wire [31:0] multiplexer_1_out, multiplexer_2_out;
  wire [31:24] _00;

  Shifter #(.width(14), .shift("lr")) shifter_1 (.in(A), .\dist (4'b0010), .out(shifter_1_out));
  Bit_Extender #(.in_width(14), .out_width(2)) bit_extender_1 (.in(A), .out(bit_extender_1_out));
  Bit_Extender #(.in_width(32), .out_width(8)) bit_extender_2 (.in(WD), .out(_00));
  Bit_Extender #(.in_width(14), .out_width(12)) bit_extender_3 (.in(shifter_1_out), .out(bit_extender_3_out));
  Multiplexer #(.width(32)) multiplexer_1 (
    .in0(WD), .in1(multiplexer_2_out), .out(multiplexer_1_out), .sel(WDOp));  // open: en
  Multiplexer #(.select(2), .width(32)) multiplexer_2 (
    .in0({_00, RDW[23:0]}), .in1({RDW[31:24], _00, RDW[15:0]}), .in2({RDW[31:16], _00, RDW[7:0]}),
    .in3({RDW[31:8], _00}), .out(multiplexer_2_out), .sel(bit_extender_1_out));  // open: en
  RAM #(.addrWidth(12), .dataWidth(32), .bus("separate")) ram_1 (
    .addr(bit_extender_3_out), .din(multiplexer_1_out), .data(RDW), .str(WE), .clk(Clk), .ld(1'b1), .clr(Rst));  // open: sel
  Subtractor #(.width(2)) subtractor_1 (.a(2'b11), .b(bit_extender_4_out), .out(subtractor_1_out));  // open: bin, bout
  Bit_Extender #(.in_width(14), .out_width(2)) bit_extender_4 (.in(A), .out(bit_extender_4_out));
  BitSelector #(.width(32), .group(8)) bitselector_1 (.in(RDW), .out(bitselector_1_out), .sel(subtractor_1_out));
  assign RDB = {{24{1'b0}}, bitselector_1_out};  // Bit_Extender bit_extender_5

  // Other names for the same wires on the sheet: _01[31:0] = {RDW[31:24], _00, RDW[15:0]};
  //   _10[31:0] = {RDW[31:16], _00, RDW[7:0]}; _11[31:0] = {RDW[31:8], _00}; WDB[7:0] = _00; _00[23:0] = RDW[23:0];
  //   _3[7:0] = RDW[7:0]; _2[7:0] = RDW[15:8]; _1[7:0] = RDW[23:16]; _0[7:0] = RDW[31:24]; WDW[31:0] = WD
endmodule

module Sll (
  input  [15:0] Imm,
  input  SllOp,
  output [31:0] SllImm
);

  wire [31:0] bit_extender_1_out, bit_extender_2_out, Op0, Op1;

  assign bit_extender_1_out = {{16{Imm[15]}}, Imm};  // Bit_Extender bit_extender_1
  assign bit_extender_2_out = {{16{1'b0}}, Imm};  // Bit_Extender bit_extender_2
  Multiplexer #(.width(32)) multiplexer_1 (.in0(Op0), .in1(Op1), .out(SllImm), .sel(SllOp));  // open: en
  Shifter #(.width(32)) shifter_1 (.in(bit_extender_1_out), .\dist (5'b00010), .out(Op0));
  Shifter #(.width(32)) shifter_2 (.in(bit_extender_2_out), .\dist (5'b10000), .out(Op1));
endmodule

module Ext (
  input  [15:0] Imm,
  output [31:0] SignImm,
  output [31:0] ZeroImm
);

  assign SignImm = {{16{Imm[15]}}, Imm};  // Bit_Extender bit_extender_1
  assign ZeroImm = {{16{1'b0}}, Imm};  // Bit_Extender bit_extender_2
endmodule

module ALU (
  input  [31:0] SrcA,
  input  [31:0] SrcB,
  input  [1:0] SelOp,
  output Zero,
  output [31:0] ALUResult
);

  wire [31:0] Op0, Op1, Op2;

  Multiplexer #(.select(2), .width(32)) multiplexer_1 (
    .in0(Op0), .in1(Op1), .in2(Op2), .out(ALUResult), .sel(SelOp));  // open: in3, en
  Comparator #(.width(32), .mode("unsigned")) comparator_1 (.a(ALUResult), .b({32{1'b0}}), .eq(Zero));  // open: gt, lt
  Adder #(.width(32)) adder_1 (.a(SrcA), .b(SrcB), .out(Op0));  // open: cin, cout
  Subtractor #(.width(32)) subtractor_1 (.a(SrcA), .b(SrcB), .out(Op1));  // open: bin, bout
  assign Op2 = SrcA | SrcB;  // OR_Gate or_1, 32 bits wide
endmodule

module Controller (
  input  [5:0] Op,
  input  [5:0] Funct,
  output [2:0] out_3,
  output out_4,
  output out_5,
  output [1:0] out_6,
  output [1:0] out_7,
  output [1:0] out_8,
  output out_9,
  output out_10,
  output out_11,
  output out_12
);

  wire and_logic1_1_alu_nop, and_logic1_1_beq, and_logic1_1_jal, and_logic1_1_lb, and_logic1_1_lui,
       and_logic1_1_lw, and_logic1_1_ori, and_logic1_1_sb, and_logic1_1_sw, and_logic2_1_add,
       and_logic2_1_beq_2, and_logic2_1_jal_2, and_logic2_1_lb_2, and_logic2_1_lui_2, and_logic2_1_lw_2,
       and_logic2_1_nop, and_logic2_1_ori_2, and_logic2_1_sb_2, and_logic2_1_sub, and_logic2_1_sw_2;

  And_Logic1 and_logic1_1 (
    .alu_nop(and_logic1_1_alu_nop), .ori(and_logic1_1_ori), .lw(and_logic1_1_lw), .sw(and_logic1_1_sw),
    .beq(and_logic1_1_beq), .lui(and_logic1_1_lui), ._31(Op[5]), ._30(Op[4]), ._29(Op[3]), ._28(Op[2]),
    ._27(Op[1]), ._26(Op[0]), .lb(and_logic1_1_lb), .sb(and_logic1_1_sb), .jal(and_logic1_1_jal));
  And_Logic2 and_logic2_1 (
    .ori(and_logic1_1_ori), .lw(and_logic1_1_lw), .sw(and_logic1_1_sw), .beq(and_logic1_1_beq),
    .lui(and_logic1_1_lui), .add(and_logic2_1_add), .sub(and_logic2_1_sub), .nop(and_logic2_1_nop),
    .ori_2(and_logic2_1_ori_2), .lw_2(and_logic2_1_lw_2), .sw_2(and_logic2_1_sw_2),
    .beq_2(and_logic2_1_beq_2), .lui_2(and_logic2_1_lui_2), ._5(Funct[5]), ._4(Funct[4]), ._3(Funct[3]),
    ._2(Funct[2]), ._1(Funct[1]), ._0(Funct[0]), .alu_nop(and_logic1_1_alu_nop), .lb(and_logic1_1_lb),
    .lb_2(and_logic2_1_lb_2), .sb(and_logic1_1_sb), .sb_2(and_logic2_1_sb_2), .jal(and_logic1_1_jal),
    .jal_2(and_logic2_1_jal_2));
  Or_logic or_logic_1 (
    .add(and_logic2_1_add), .sub(and_logic2_1_sub), .nop(and_logic2_1_nop), .ori(and_logic2_1_ori_2),
    .lw(and_logic2_1_lw_2), .sw(and_logic2_1_sw_2), .beq(and_logic2_1_beq_2), .lui(and_logic2_1_lui_2),
    .lb(and_logic2_1_lb_2), .sb(and_logic2_1_sb_2), .jal(and_logic2_1_jal_2), .MemWrite(out_4),
    .ALUControl(out_6), .ALUSrc(out_7), .RegDst(out_8), .RegWrite(out_9), .SllOp(out_10), .out_21(out_11),
    .MemtoReg(out_3), .Branch(out_5), .jalSel(out_12));
endmodule

module And_Logic1 (
  input  _31,
  input  _30,
  input  _29,
  input  _28,
  input  _27,
  input  _26,
  output alu_nop,
  output ori,
  output lw,
  output sw,
  output beq,
  output lui,
  output lb,
  output sb,
  output jal
);

  wire not_1_out, not_2_out, not_3_out, not_4_out, not_5_out, not_6_out;

  not not_1 (not_1_out, _31);
  not not_2 (not_2_out, _29);
  not not_3 (not_3_out, _30);
  not not_4 (not_4_out, _28);
  not not_5 (not_5_out, _26);
  not not_6 (not_6_out, _27);
  and u_ALU_NOP (alu_nop, not_1_out, not_3_out, not_2_out, not_4_out, not_6_out, not_5_out);
  and u_ORI (ori, not_1_out, not_3_out, _29, _28, not_6_out, _26);
  and u_LW (lw, _31, not_3_out, not_2_out, not_4_out, _27, _26);
  and u_SW (sw, _31, not_3_out, _29, not_4_out, _27, _26);
  and u_BEQ (beq, not_1_out, not_3_out, not_2_out, _28, not_6_out, not_5_out);
  and u_LUI (lui, not_1_out, not_3_out, _29, _28, _27, _26);
  and u_LB (lb, _31, not_3_out, not_2_out, not_4_out, not_6_out, not_5_out);
  and u_SB (sb, _31, not_3_out, _29, not_4_out, not_6_out, not_5_out);
  and u_JAL (jal, not_1_out, not_3_out, not_2_out, not_4_out, _27, _26);
endmodule

module And_Logic2 (
  input  _5,
  input  _4,
  input  _3,
  input  _2,
  input  _1,
  input  _0,
  input  alu_nop,
  input  ori,
  input  lw,
  input  sw,
  input  beq,
  input  lui,
  input  lb,
  input  sb,
  input  jal,
  output add,
  output sub,
  output nop,
  output ori_2,
  output lw_2,
  output sw_2,
  output beq_2,
  output lui_2,
  output lb_2,
  output sb_2,
  output jal_2
);

  wire not_1_out, not_2_out, not_3_out, not_4_out, not_5_out, not_6_out, not_7_out;

  not not_1 (not_1_out, _5);
  not not_2 (not_2_out, _4);
  not not_3 (not_3_out, _3);
  not not_4 (not_4_out, _2);
  not not_5 (not_5_out, _0);
  not not_6 (not_6_out, _1);
  not not_7 (not_7_out, alu_nop);
  and u_ADD (add, _5, not_2_out, not_3_out, alu_nop, not_4_out, not_6_out, not_5_out);
  and u_SUB (sub, _5, not_2_out, not_3_out, alu_nop, not_4_out, _1, not_5_out);
  and u_NOP (nop, not_1_out, not_2_out, not_3_out, alu_nop, not_4_out, not_6_out, not_5_out);

  assign beq_2 = beq;
  assign jal_2 = jal;
  assign lb_2 = lb;
  assign lui_2 = lui;
  assign lw_2 = lw;
  assign ori_2 = ori;
  assign sb_2 = sb;
  assign sw_2 = sw;
endmodule

module Or_logic (
  input  add,
  input  sub,
  input  nop,
  input  ori,
  input  lw,
  input  sw,
  input  beq,
  input  lui,
  input  lb,
  input  sb,
  input  jal,
  output [2:0] MemtoReg,
  output MemWrite,
  output jalSel,
  output Branch,
  output [1:0] ALUControl,
  output [1:0] ALUSrc,
  output [1:0] RegDst,
  output RegWrite,
  output SllOp,
  output out_21
);

  buf MemtoReg2 (MemtoReg[2], jal);  // OR_Gate
  or MemtoReg1 (MemtoReg[1], lui, lb);
  or MemtoReg0 (MemtoReg[0], lw, lb);
  or u_MemWrite (MemWrite, sw, sb);
  buf u_jalSel (jalSel, jal);  // OR_Gate
  buf u_Branch (Branch, beq);  // OR_Gate
  buf ALUControl1 (ALUControl[1], ori);  // OR_Gate
  or ALUControl0 (ALUControl[0], sub, beq);
  buf ALUSrc1 (ALUSrc[1], ori);  // OR_Gate
  or ALUSrc0 (ALUSrc[0], lw, lb, sb, sw);
  buf RegDst1 (RegDst[1], jal);  // OR_Gate
  or RegDst0 (RegDst[0], add, sub);
  or u_RegWrite (RegWrite, jal, add, sub, ori, lw, lui, lb);
  buf u_SllOp (SllOp, lui);  // OR_Gate
  buf WDOp (out_21, sb);  // OR_Gate
endmodule
